# Fritzing sketch Animatronic 10ch_iBus (saved by Fritzing 0.9.3b)

parts:
  J7 = male pin header, 3 pins [form="♂ (male)"]  # not connected
  J5 = male pin header, 3 pins [form="♂ (male)"]  # not connected
  J6 = male pin header, 3 pins [form="♂ (male)"]  # not connected
  J4 = male pin header, 3 pins [form="♂ (male)"]  # not connected
  J8 = male pin header, 3 pins [form="♂ (male)"]  # not connected
  J3 = male pin header, 3 pins [form="♂ (male)"]  # not connected
  J9 = male pin header, 3 pins [form="♂ (male)"]  # not connected
  Part2 = Arduino Nano (Rev3.0)
  Part3 = 16-Channel 12-bit PWM Servo Driver - I2C [part_number=815]
  J10 = Basic Servo
  J11 = Basic Servo
  J12 = Basic Servo
  J13 = Basic Servo
  JACK1 = 2.1mm Barrel Jack with Terminal Block
  J14 = Basic Servo
  J15 = Basic Servo
  J16 = Basic Servo
  J17 = Basic Servo
  J18 = Basic Servo
  J19 = Basic Servo

nets:
  GND: Part2.GND, Part3.GND, J10.gnd, J11.gnd, J12.gnd, J13.gnd, JACK1.NEG, J14.gnd, J15.gnd, J16.gnd, J17.gnd, J18.gnd, J19.gnd
  5V: Part2.5V, Part3.VCC
  N1: Part2.A5, Part3.SCL
  N2: Part2.A4, Part3.SDA
  N3: Part3.PWRIN, JACK1.POS
  N4: Part3.PWM7, J17.pulse
  VCC: Part3.5.0V, J10.vcc, J11.vcc, J12.vcc, J13.vcc, J14.vcc, J15.vcc, J16.vcc, J17.vcc, J18.vcc, J19.vcc
  N5: Part3.PWM6, J16.pulse
  N6: Part3.PWM5, J15.pulse
  N7: Part3.PWM4, J14.pulse
  N8: Part3.PWM3, J13.pulse
  N9: Part3.PWM2, J12.pulse
  N10: Part3.PWM1, J11.pulse
  N11: Part3.PWM0, J10.pulse
  N12: Part3.PWM9, J19.pulse
  N13: Part3.PWM8, J18.pulse

notes:
  PCA9685 16-channel PWM controller uses I2C interface:
  SDA to Arduino A4
  SCL to Arduino A5
  VCC to Arduino 5V
  GND to Arduino GND
  External 5V DC power supply for servos
  FS-IA6B iBus connections
  ---
  Yellow - Signal - Arduino 8
  Red - VCC - Arduino 5V
  Black - GND - Arduino GND
  FS-IA6B iBus connection gives serial output of all 14-channels which can be read on an emulated serial connection on an Arduino GPIO pin.

custom parts:
  16-Channel 12-bit PWM Servo Driver - I2C: You want to make a cool robot, maybe a hexapod walker, or maybe just a piece of art with a lot of moving parts. Or maybe you want to drive a lot of LEDs with precise PWM output. Using only two pins, control 16 free-running PWM outputs! You can even chain up 62 breakouts to control up to 992 PWM outputs.
