# Fritzing sketch Animatronic 10ch_iBus_ESP32 (saved by Fritzing 0.9.4)

parts:
  Part3 = 16-Channel 12-bit PWM Servo Driver - I2C [part_number=815]
  J10 = Basic Servo
  J11 = Basic Servo
  J12 = Basic Servo
  J13 = Basic Servo
  JACK1 = 2.1mm Barrel Jack with Terminal Block
  J14 = Basic Servo
  J15 = Basic Servo
  J16 = Basic Servo
  J17 = Basic Servo
  J18 = Basic Servo
  J19 = Basic Servo
  U1 = ESP32S-HiLetgo [part_number=ESP32S-HiLetgo]

nets:
  N1: Part3.PWRIN, JACK1.POS
  GND: Part3.GND, J10.gnd, J11.gnd, J12.gnd, J13.gnd, JACK1.NEG, J14.gnd, J15.gnd, J16.gnd, J17.gnd, J18.gnd, J19.gnd, U1.GND
  N2: Part3.PWM7, J17.pulse
  VCC: Part3.5.0V, J10.vcc, J11.vcc, J12.vcc, J13.vcc, J14.vcc, J15.vcc, J16.vcc, J17.vcc, J18.vcc, J19.vcc
  N3: Part3.PWM6, J16.pulse
  N4: Part3.PWM5, J15.pulse
  N5: Part3.PWM4, J14.pulse
  N6: Part3.PWM3, J13.pulse
  N7: Part3.PWM2, J12.pulse
  N8: Part3.PWM1, J11.pulse
  N9: Part3.PWM0, J10.pulse
  N10: Part3.VCC, U1.3.3
  N11: Part3.SDA, U1.GPIO21
  N12: Part3.SCL, U1.GPIO22
  N13: Part3.PWM9, J19.pulse
  N14: Part3.PWM8, J18.pulse

notes:
  PCA9685 16-channel PWM controller uses I2C interface. It can operate at 3.3V level of the ESP32, and had built-in pullups on the SDA and SCL lines so no external resistors are required.
  SDA to ESP32 GPIO 21
  SCL to ESP32 GPIO 22
  VCC to ESP32 3.3V
  GND to ESP32 GND
  External 5V DC power supply for servos
  FS-IA6B iBus connections
  ---
  Yellow - Signal - ESP32 GPIO16 (Serial2 Rx)
  Red - VCC - ESP32 VIn (5V)
  Black - GND - ESP32 GND
  FS-IA6B iBus connection gives serial output of all 14-channels which can be read on a UART GPIO pin on the ESP32.

custom parts:
  16-Channel 12-bit PWM Servo Driver - I2C: You want to make a cool robot, maybe a hexapod walker, or maybe just a piece of art with a lot of moving parts. Or maybe you want to drive a lot of LEDs with precise PWM output. Using only two pins, control 16 free-running PWM outputs! You can even chain up 62 breakouts to control up to 992 PWM outputs.
  ESP32S-HiLetgo: HiLetgo ESP-WROOM-32 ESP32 ESP-32S Development Board 2.4GHz Dual-Mode WiFi + Bluetooth Dual Cores Microcontroller The ESP32 integrated with Antenna switches, RF Balun, power amplifiers, low-noise amplifiers, filters, and management modules, and the entire solution occupies the least area of PCB. 2.4 GHz Wi-Fi plus Bluetooth dual-mode chip, with TSMC Ultra-low power consumption 40nm technology,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
