# Fritzing sketch Animatronic_6ch_PWM (saved by Fritzing 0.9.3b)

parts:
  J7 = male pin header, 3 pins [form="♂ (male)"]
  J5 = male pin header, 3 pins [form="♂ (male)"]
  J6 = male pin header, 3 pins [form="♂ (male)"]
  J4 = male pin header, 3 pins [form="♂ (male)"]
  J8 = male pin header, 3 pins [form="♂ (male)"]
  J3 = male pin header, 3 pins [form="♂ (male)"]
  J9 = male pin header, 3 pins [form="♂ (male)"]
  Part2 = Arduino Nano (Rev3.0)
  Part3 = 16-Channel 12-bit PWM Servo Driver - I2C [part_number=815]
  J10 = Basic Servo
  J11 = Basic Servo
  J12 = Basic Servo
  J13 = Basic Servo
  JACK1 = 2.1mm Barrel Jack with Terminal Block
  J14 = Basic Servo
  J15 = Basic Servo

nets:
  N1: J7.pin1, Part2.D6
  5V: J5.pin2, Part2.5V, Part3.VCC
  GND: J5.pin3, Part2.GND, Part3.GND, J10.gnd, J11.gnd, J12.gnd, J13.gnd, JACK1.NEG, J14.gnd, J15.gnd
  N2: J6.pin1, Part2.D2
  N3: J4.pin1, Part2.D3
  N4: J8.pin1, Part2.D4
  N5: J3.pin1, Part2.D5
  N6: J9.pin1, Part2.D7
  N7: Part2.A5, Part3.SCL
  N8: Part2.A4, Part3.SDA
  N9: Part3.PWRIN, JACK1.POS
  N10: Part3.PWM5, J15.pulse
  VCC: Part3.5.0V, J10.vcc, J11.vcc, J12.vcc, J13.vcc, J14.vcc, J15.vcc
  N11: Part3.PWM4, J14.pulse
  N12: Part3.PWM3, J13.pulse
  N13: Part3.PWM2, J12.pulse
  N14: Part3.PWM1, J11.pulse
  N15: Part3.PWM0, J10.pulse

notes:
  PCA9685 16-channel PWM controller uses I2C interface:
  SDA to Arduino A4
  SCL to Arduino A5
  VCC to Arduino 5V
  GND to Arduino GND
  External 5V DC power supply for servos
  FS-IA6 6-channel receiver
  FS-IA6 gives PWM output for each channel, which can be read on Arduino GPIO pin:
  FS-IA6 "S" (ch1-ch6) to Arduino pins 2-7
  FS-IA6 "-" to Arduino GND
  FS-IA6 "+" to Arduino 5V

custom parts:
  16-Channel 12-bit PWM Servo Driver - I2C: You want to make a cool robot, maybe a hexapod walker, or maybe just a piece of art with a lot of moving parts. Or maybe you want to drive a lot of LEDs with precise PWM output. Using only two pins, control 16 free-running PWM outputs! You can even chain up 62 breakouts to control up to 992 PWM outputs.
