# Fritzing sketch FS-i6 Arduino FIrmware Mod (saved by Fritzing 0.9.3b)
breadboards: 1

parts:
  Part1 = Arduino Nano (Rev3.0)
  R1 = Resistor [tolerance=±5% resistance=2.2k package=THT]

nets:
  N1: Part1.D0/RX, R1.Pin_1
  N2: Part1.RESET, Part1.GND, R1.Pin_0

notes:
  Black wire touching metal sleeve of trainer socket to Arduino GND
  Yellow wire connected to Pin 3 of trainer socket (bottom left) to Arduino TX
  Green wire connected to Pin 4 of trainer socket (bottom right) to Arduino RX
  1
  2
  3
  4
  Sleeve
  2.2kΩ pull-down resistor between Arduino RX and GND
  Jumper connecting Arduino RST and GND bypasses processor, effectively causing Arduino to act as a Serial-TTL convertor
